# Fritzing sketch CT2_FA (saved by Fritzing 0.9.3b)

parts:
  Componente1 = Arduino MKR WIFI 1010
  Part1 = MCP9808
  2_Channel_Relay1 = 2 Channel Power Relay
  OLED1 = 128x32 I2C Monochrome OLED Display
  L1 = Solenoid
  RE2 = Rotary Encoder [package=THT]

nets:
  N1: Componente1.D8/MOSI, 2_Channel_Relay1.IN1
  N2: Componente1.D11/SDA, Part1.SDA, OLED1.SDA
  N3: Componente1.D12/SCL, Part1.SCL, OLED1.SCL
  GND: Componente1.GND, Part1.GND, 2_Channel_Relay1.GND, OLED1.GND, RE2.EncoderPinC, RE2.SwitchrPinD
  N4: Componente1.D5_PWM, RE2.EncoderPinA
  N5: Componente1.D6, RE2.EncoderPinB
  N6: Componente1.D7, RE2.SwitchPinE
  N7: 2_Channel_Relay1.JD-VCC, 2_Channel_Relay1.VCC#9
  N8: 2_Channel_Relay1.K1-COM, L1.pin1
  N9: 2_Channel_Relay1.K1-NO, L1.pin2

custom parts:
  Arduino MKR WIFI 1010: The MKR WIFI 1010 is a significant improvement on the MKR 1000 WIFI. It's equipped with an ESP32 module made by U-BLOX. This board aims to speed up and simplify the prototyping of WiFi based IoT applications thanks to the flexibility of the ESP32 module and its low power consumption. The board is composed of three main blocks: SAMD21 Cortex-M0+ 32bit Low Power ARM MCU; U-BLOX NINA-W10 Series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
  2 Channel Power Relay: A 2 channel power relay. The module operates at 5V.
  Rotary Encoder: Rotary Encoder from ALPSec11e with switch. This version has an alternate (which has been used in boards) pcb footprint from @opera_night in the forums. It is probably the best one to start from to see if you part matches.
